# Fritzing sketch rangkaianNode (saved by Fritzing 0.9.3b)

parts:
  D2 = Rectifier Diode [part_number=1N4001 package="300 mil [THT]"]  # not connected
  ESP32_DEVKIT2 = MH-ET LIVE ESP32 DEVKIT 38 pins
  STEP_DOWN1 = DC-DC Power Module (5v)  # not connected
  LED3 = smd LED [color="Red (633nm)" package="1206 [SMD]"]
  LED4 = smd LED [color="Red (633nm)" package="0805 [SMD]"]
  Panel_PLTS_20_WP1 = Solar Panel [package="Renogy 50 Watts 12 Volt Monocrystalline Bendable Solar Panel"]  # not connected
  BATTERY1 = 12 battery [package=battery]  # not connected
  Part2 = Solar Charge Controller [part_number="HGX Series Solar Charge Controller PWM" package=PWM-Model]  # not connected
  LoRa_SX1279 = Osoyoo SX1278-ra-02
  AM1 = AM2302 Humidity and Temperature Sensor  # not connected
  부품3 = FC-28 Soil Hygrometer Module - Probe  # not connected
  부품4 = FC-28 Soil Hygrometer Module  # not connected
  S2 = Reed switch [package=THT]  # not connected
  R2 = Resistor [tolerance=±5% resistance=10k package=THT]  # not connected

nets:
  N1: ESP32_DEVKIT2.IO26, LED3.anode
  N2: ESP32_DEVKIT2.IO27, LED4.anode
  N3: ESP32_DEVKIT2.IO14, LoRa_SX1279.RST
  N4: ESP32_DEVKIT2.IO23, LoRa_SX1279.MOSI
  N5: ESP32_DEVKIT2.IO19, LoRa_SX1279.MISO
  N6: ESP32_DEVKIT2.IO18, LoRa_SX1279.SCK
  N7: ESP32_DEVKIT2.IO5, LoRa_SX1279.NSS
  N8: ESP32_DEVKIT2.IO2, LoRa_SX1279.DIO0

custom parts:
  MH-ET LIVE ESP32 DEVKIT 38 pins: http://mh.nodebb.com/topic/2/mh-et-live-esp32-devkit
  DC-DC Power Module (5v): DC-DC Power Module based con AMS1117-5.0 Input: DC 6~12V (input power must higher 1V than output power); Output: 5V (+/-0.05V error), 800mA
  Solar Panel: Renogy 50 Watts 12 Volt Solar Panel
  12 battery: 12V lead acid type battery, like the Husqvarna YTH2448 12V 35AH battery. This is the mini version 1/4 the size of the actual battery to be closer to typical breadboard parts (around 2in wide rathher than 7in). The pads in pcb are sized to accomidate up to 14ga wire (as these batterys will deliver high currents.)
  Solar Charge Controller: PWM-Solar Charge Controller
  Osoyoo SX1278-ra-02: Osoyoo Long Distance wireless transceiver Uart LoRa Module.
  FC-28 Soil Hygrometer Module - Probe: The FC-28 is a soil hygrometer module that uses the Texas Instruments LM393 comparator chip to provide an analog measurement of soil humidity.
  FC-28 Soil Hygrometer Module: The FC-28 is a soil hygrometer module that uses the Texas Instruments LM393 comparator chip to provide an analog measurement of soil humidity. The digital output is high when soil moisture is over a certain threshold, as determined by adjusting the potentiometer.
